// Logisim project IT012_Lab01_25520559.circ as structural Verilog
module Warmup (
  input  A,
  input  B,
  output F
);

  wire not_1_out;

  not not_1 (not_1_out, B);
  and and_1 (F, A, not_1_out);
endmodule

module TN1 (
  input  A,
  input  B,
  input  C,
  output NOT_output,
  output AND_output,
  output OR_output,
  output NAND_output,
  output NOR_output,
  output XOR_output,
  output XNOR_output,
  output XOR3,
  output NAND3,
  output CHAIN
);

  wire nand_1_out;

  nand nand_1 (nand_1_out, A, A);
  not not_1 (NOT_output, A);
  and and_1 (AND_output, A, A);
  or or_1 (OR_output, A, A);
  nand nand_2 (NAND_output, A, A);
  nor nor_1 (NOR_output, A, A);
  xor xor_1 (XOR_output, A, A);
  nand nand_3 (CHAIN, nand_1_out, C);
  xnor xnor_1 (XNOR_output, A, A);
  xor xor_2 (XOR3, A, A, C);
  nand nand_4 (NAND3, A, A, C);

  assign B = A;
endmodule

module TN2 (
  input  x,
  input  y,
  input  z,
  output EQ1,
  output EQ2,
  output EQ3,
  output EQ4,
  output EQ5
);

  wire and_1_out, and_2_out, and_3_out, and_4_out, and_5_out, not_1_out, not_2_out, not_3_out, not_4_out,
       not_5_out, or_1_out, or_2_out, or_3_out, or_4_out;

  not not_1 (not_1_out, x);
  not not_2 (not_2_out, y);
  not not_3 (not_3_out, x);
  or or_1 (or_1_out, x, y);
  and and_1 (and_1_out, not_1_out, not_2_out);
  and and_2 (and_2_out, x, y);
  or or_2 (or_2_out, x, z);
  and and_3 (and_3_out, y, z);
  and and_4 (and_4_out, not_3_out, y);
  not not_4 (not_4_out, or_1_out);
  not not_5 (not_5_out, and_2_out);
  and and_5 (and_5_out, or_1_out, or_2_out);
  or or_3 (or_3_out, x, and_3_out);
  or or_4 (or_4_out, x, and_4_out);
  xnor xnor_1 (EQ1, not_4_out, and_1_out);
  xnor xnor_2 (EQ2, and_1_out, not_5_out);
  xnor xnor_3 (EQ3, and_5_out, or_3_out);
  xnor xnor_4 (EQ4, x, or_4_out);
  xnor xnor_5 (EQ5, or_4_out, or_1_out);
endmodule

module TN3 (
  input  A,
  input  B,
  input  C,
  input  D,
  output F
);

  wire and_1_out, and_2_out, and_3_out, and_4_out, and_5_out, and_6_out, not_1_out, not_2_out, not_3_out,
       not_4_out;

  not not_1 (not_1_out, A);
  not not_2 (not_2_out, B);
  not not_3 (not_3_out, C);
  not not_4 (not_4_out, D);
  and and_1 (and_1_out, not_1_out, not_2_out, C, not_4_out);
  and and_2 (and_2_out, not_1_out, not_2_out, C, D);
  and and_3 (and_3_out, not_1_out, B, not_3_out, D);
  and and_4 (and_4_out, not_1_out, B, C, D);
  and and_5 (and_5_out, A, not_2_out, C, D);
  and and_6 (and_6_out, A, B, not_3_out, D);
  or or_1 (F, and_1_out, and_2_out, and_3_out, and_4_out, and_5_out, and_6_out);
endmodule

module TN4 (
  input  A,
  input  B,
  input  C,
  input  D,
  output F_can,
  output EQ1,
  output F_sop,
  output EQ2,
  output F_pos
);

  wire and_1_out, and_2_out, and_3_out, and_4_out, and_5_out, and_6_out, and_7_out, and_8_out, and_9_out,
       and_10_out, not_1_out, not_2_out, not_3_out, not_4_out, or_1_out, or_2_out, or_3_out, or_4_out;

  not not_1 (not_1_out, A);
  not not_2 (not_2_out, B);
  not not_3 (not_3_out, C);
  not not_4 (not_4_out, D);
  or or_1 (or_1_out, B, C);
  or or_2 (or_2_out, not_1_out, D);
  or or_3 (or_3_out, not_2_out, D);
  or or_4 (or_4_out, not_1_out, not_2_out, not_3_out);
  and and_1 (and_1_out, not_1_out, not_2_out, C, not_4_out);
  and and_2 (and_2_out, not_1_out, not_2_out, C, D);
  and and_3 (and_3_out, not_1_out, B, not_3_out, D);
  and and_4 (and_4_out, not_1_out, B, C, D);
  and and_5 (and_5_out, A, not_2_out, C, D);
  and and_6 (and_6_out, A, B, not_3_out, D);
  and and_7 (and_7_out, not_1_out, not_2_out, C);
  and and_8 (and_8_out, not_2_out, C, D);
  and and_9 (and_9_out, B, not_3_out, D);
  and and_10 (and_10_out, not_1_out, C, D);
  and and_11 (F_pos, or_1_out, or_2_out, or_3_out, or_4_out);
  or or_5 (F_can, and_1_out, and_2_out, and_3_out, and_4_out, and_5_out, and_6_out);
  or or_6 (F_sop, and_7_out, and_8_out, and_9_out, and_10_out);
  xnor xnor_1 (EQ1, F_can, F_sop);
  xnor xnor_2 (EQ2, F_can, F_pos);
endmodule

module TN5 (
  input  A,
  input  B,
  input  C,
  output F
);

  wire xor_1_out;

  xor xor_1 (xor_1_out, A, B);
  xor xor_2 (F, xor_1_out, C);
endmodule

module TN1v1 (
  input  A,
  input  B,
  input  C,
  output NOT_gate,
  output AND_gate,
  output OR_gate,
  output NAND_gate,
  output NOR_gate,
  output XOR_gate,
  output XNOR_gate,
  output XOR3,
  output NAND3,
  output CHAIN
);

  wire nand_3_out;

  not not_1 (NOT_gate, A);
  and and_1 (AND_gate, A, B);
  or or_1 (OR_gate, A, B);
  nand nand_1 (NAND_gate, A, B);
  nor nor_1 (NOR_gate, A, B);
  xor xor_1 (XOR_gate, A, B);
  xnor xnor_1 (XNOR_gate, A, B);
  xor xor_2 (XOR3, A, B, C);
  nand nand_2 (NAND3, A, B, C);
  nand nand_3 (nand_3_out, A, B);
  nand nand_4 (CHAIN, nand_3_out, C);
endmodule
